// Logisim project Lab_6_cybernetica.circ as structural Verilog: 9 circuits, main circuit SR триггер
module Lab_6 (
  input  \SR_триггер ,
  input  in_2,
  input  in_3,
  input  in_4,
  input  in_5,
  input  in_6,
  input  in_7,
  input  in_8,
  input  in_9,
  input  in_10,
  input  in_11,
  input  in_12,
  input  in_13,
  input  in_14,
  input  in_15,
  input  in_16,
  input  in_17,
  input  in_18,
  input  in_19,
  input  \T_триггер ,
  input  \JK_триггер ,
  input  in_22,
  input  in_23,
  input  in_24,
  input  in_25,
  input  in_26,
  input  in_27,
  input  in_28,
  output out_29,
  output out_30,
  output out_31,
  output out_32,
  output out_33,
  output out_34,
  output out_35,
  output out_36,
  output out_37,
  output out_38,
  output out_39,
  output out_40,
  output out_41,
  output out_42
);

  wire not_1_out, not_2_out, \детектор_переднего_фронта_1_out_2 , \детектор_переднего_фронта_2_out_2 ;

  \SR_триггер  \sr_триггер_1  (.in_1(\SR_триггер ), .in_2(in_4), .in_3(in_7), .out_4(out_29), .out_5(out_32));
  \T_триггер  \t_триггер_1  (.T(in_23), .in_3(in_25), .out_5(out_39), .out_6(out_41), .in_1(\T_триггер ), .in_4(in_27));
  \Детектор_переднего_фронта  \u_детектор_переднего_фронта_1  (
    .in_1(in_16), .out_2(\детектор_переднего_фронта_1_out_2 ));
  \D_триггер  \d_триггер_1  (.in_2(in_5), .in_3(in_8), .out_5(out_30), .out_6(out_33), .in_1(in_2), .in_4(in_10));
  \D_триггер  \d_триггер_2  (
    .in_2(in_14), .in_3(\детектор_переднего_фронта_1_out_2 ), .out_5(out_35), .out_6(out_37), .in_1(in_12),
    .in_4(in_18));
  \JK_триггер  \jk_триггер_1  (
    .in_2(in_22), .in_3(in_24), .in_4(in_26), .out_6(out_40), .out_7(out_42), .in_1(\JK_триггер ),
    .in_5(in_28));
  not not_1 (not_1_out, in_9);
  \Детектор_переднего_фронта  \u_детектор_переднего_фронта_2  (
    .in_1(not_2_out), .out_2(\детектор_переднего_фронта_2_out_2 ));
  not not_2 (not_2_out, in_17);
  \D_триггер  \d_триггер_3  (.in_2(in_6), .in_3(not_1_out), .out_5(out_31), .out_6(out_34), .in_1(in_3), .in_4(in_11));
  \D_триггер  \d_триггер_4  (
    .in_2(in_15), .in_3(\детектор_переднего_фронта_2_out_2 ), .out_5(out_36), .out_6(out_38), .in_1(in_13),
    .in_4(in_19));

  // Notes on the sheet:
  //   D триггер (верхний уровень)
  //   D триггер (передний фронт)
  //   D триггер (нижний уровень)
  //   D триггер (задний фронт)
  //   Бинарный счётчик
endmodule

module \SR_триггер  (
  input  in_1,
  input  in_2,
  input  in_3,
  output out_4,
  output out_5
);

  wire nand_1_out, nand_2_out;

  nand nand_1 (nand_1_out, in_1, in_2);
  nand nand_2 (nand_2_out, in_2, in_3);
  nand nand_3 (out_4, nand_1_out, out_5);
  nand nand_4 (out_5, out_4, nand_2_out);
endmodule

module \D_триггер  (
  input  in_1,
  input  in_2,
  input  in_3,
  input  in_4,
  output out_5,
  output out_6
);

  wire nand_1_out, nand_2_out;

  nand nand_1 (nand_1_out, in_2, in_3);
  nand nand_2 (nand_2_out, in_3, ~in_2);  // NAND_Gate
  nand nand_3 (out_5, ~in_1, nand_1_out, out_6);  // NAND_Gate
  nand nand_4 (out_6, out_5, nand_2_out, ~in_4);  // NAND_Gate
endmodule

module \Детектор_переднего_фронта  (
  input  in_1,
  output out_2
);

  wire not_1_out, not_2_out, not_3_out;

  not not_1 (not_1_out, in_1);
  not not_2 (not_2_out, not_3_out);
  not not_3 (not_3_out, not_1_out);
  and and_1 (out_2, not_2_out, in_1);
endmodule

module \T_триггер  (
  input  in_1,
  input  T,
  input  in_3,
  input  in_4,
  output out_5,
  output out_6
);

  wire xor_1_out, \детектор_переднего_фронта_1_out_2 ;

  xor xor_1 (xor_1_out, out_5, T);
  \Детектор_переднего_фронта  \u_детектор_переднего_фронта_1  (
    .in_1(in_3), .out_2(\детектор_переднего_фронта_1_out_2 ));
  \D_триггер  \d_триггер_1  (
    .in_2(xor_1_out), .in_3(\детектор_переднего_фронта_1_out_2 ), .out_5(out_5), .out_6(out_6), .in_1(in_1),
    .in_4(in_4));
endmodule

module \JK_триггер  (
  input  in_1,
  input  in_2,
  input  in_3,
  input  in_4,
  input  in_5,
  output out_6,
  output out_7
);

  wire and_1_out, and_2_out, not_1_out, or_1_out, \детектор_переднего_фронта_1_out_2 ;

  not not_1 (not_1_out, in_3);
  and and_1 (and_1_out, out_7, in_2);
  or or_1 (or_1_out, and_1_out, and_2_out);
  and and_2 (and_2_out, not_1_out, out_6);
  \Детектор_переднего_фронта  \u_детектор_переднего_фронта_1  (
    .in_1(in_4), .out_2(\детектор_переднего_фронта_1_out_2 ));
  \D_триггер  \d_триггер_1  (
    .in_2(or_1_out), .in_3(\детектор_переднего_фронта_1_out_2 ), .out_5(out_6), .out_6(out_7), .in_1(in_1),
    .in_4(in_5));
endmodule

module \Счётчик_4_бит  (
  input  Enable,
  input  Clock,
  input  in_3,
  output [3:0] out_4
);

  wire and_1_out, and_2_out, and_3_out;

  and and_1 (and_1_out, Enable, Clock);
  \T_триггер  \t_триггер_1  (.T(1'b1), .in_3(and_1_out), .out_5(out_4[0]), .in_1(1'b0), .in_4(in_3));  // open: out_6
  \T_триггер  \t_триггер_2  (
    .T(out_4[0]), .in_3(and_1_out), .out_5(out_4[1]), .in_1(1'b0), .in_4(in_3));  // open: out_6
  and and_2 (and_2_out, out_4[0], out_4[1]);
  \T_триггер  \t_триггер_3  (
    .T(and_2_out), .in_3(and_1_out), .out_5(out_4[2]), .in_1(1'b0), .in_4(in_3));  // open: out_6
  and and_3 (and_3_out, and_2_out, out_4[2]);
  \T_триггер  \t_триггер_4  (
    .T(and_3_out), .in_3(and_1_out), .out_5(out_4[3]), .in_1(1'b0), .in_4(in_3));  // open: out_6
endmodule

module \Улучшенный_счётчик_8_бит  (
  input  Clock,
  input  \Счёт_вверх_вниз ,
  input  Enable,
  input  \Сброс ,
  input  \Запись ,
  input  [7:0] in_6,
  output [7:0] out_7
);

  wire and_1_out, and_2_out, and_3_out, and_4_out, and_5_out, and_6_out, and_7_out, and_8_out, and_9_out,
       and_10_out, and_11_out, and_12_out, and_13_out, and_14_out, demultiplexer_1_out0,
       demultiplexer_1_out1, demultiplexer_2_out0, demultiplexer_2_out1, demultiplexer_3_out0,
       demultiplexer_3_out1, demultiplexer_4_out0, demultiplexer_4_out1, demultiplexer_5_out0,
       demultiplexer_5_out1, demultiplexer_6_out0, demultiplexer_6_out1, demultiplexer_7_out0,
       demultiplexer_7_out1, demultiplexer_8_out0, demultiplexer_8_out1, or_1_out, or_2_out, or_3_out,
       or_4_out, or_5_out, or_6_out, or_7_out, or_8_out, or_9_out, or_10_out, or_11_out, or_12_out,
       or_13_out, or_14_out, or_15_out, t_ff_1_qn, t_ff_2_qn, t_ff_3_qn, t_ff_4_qn, t_ff_5_qn, t_ff_6_qn,
       t_ff_7_qn;

  T_Flip_Flop t_ff_1 (
    .clk(Clock), .T(1'b1), .Q(out_7[0]), .Qn(t_ff_1_qn), .preset(demultiplexer_1_out1), .reset(or_1_out),
    .en(Enable));
  or or_1 (or_1_out, demultiplexer_1_out0, \Сброс );
  Demultiplexer #(.disabled(0)) demultiplexer_1 (
    .out0(demultiplexer_1_out0), .out1(demultiplexer_1_out1), .in(\Запись ), .sel(in_6[0]));  // open: en
  and and_1 (and_1_out, \Счёт_вверх_вниз , out_7[0]);
  and and_2 (and_2_out, t_ff_1_qn, ~\Счёт_вверх_вниз );  // AND_Gate
  T_Flip_Flop t_ff_2 (
    .clk(Clock), .T(or_2_out), .Q(out_7[1]), .Qn(t_ff_2_qn), .preset(demultiplexer_2_out1), .reset(or_3_out),
    .en(Enable));
  or or_2 (or_2_out, and_1_out, and_2_out);
  or or_3 (or_3_out, demultiplexer_2_out0, \Сброс );
  Demultiplexer #(.disabled(0)) demultiplexer_2 (
    .out0(demultiplexer_2_out0), .out1(demultiplexer_2_out1), .in(\Запись ), .sel(in_6[1]));  // open: en
  and and_3 (and_3_out, and_1_out, out_7[1]);
  and and_4 (and_4_out, t_ff_2_qn, and_2_out);
  T_Flip_Flop t_ff_3 (
    .clk(Clock), .T(or_4_out), .Q(out_7[2]), .Qn(t_ff_3_qn), .preset(demultiplexer_3_out1), .reset(or_5_out),
    .en(Enable));
  or or_4 (or_4_out, and_3_out, and_4_out);
  or or_5 (or_5_out, demultiplexer_3_out0, \Сброс );
  Demultiplexer #(.disabled(0)) demultiplexer_3 (
    .out0(demultiplexer_3_out0), .out1(demultiplexer_3_out1), .in(\Запись ), .sel(in_6[2]));  // open: en
  and and_5 (and_5_out, and_3_out, out_7[2]);
  and and_6 (and_6_out, t_ff_3_qn, and_4_out);
  T_Flip_Flop t_ff_4 (
    .clk(Clock), .T(or_6_out), .Q(out_7[3]), .Qn(t_ff_4_qn), .preset(demultiplexer_4_out1), .reset(or_7_out),
    .en(Enable));
  or or_6 (or_6_out, and_5_out, and_6_out);
  or or_7 (or_7_out, demultiplexer_4_out0, \Сброс );
  Demultiplexer #(.disabled(0)) demultiplexer_4 (
    .out0(demultiplexer_4_out0), .out1(demultiplexer_4_out1), .in(\Запись ), .sel(in_6[3]));  // open: en
  and and_7 (and_7_out, and_5_out, out_7[3]);
  and and_8 (and_8_out, t_ff_4_qn, and_6_out);
  T_Flip_Flop t_ff_5 (
    .clk(Clock), .T(or_8_out), .Q(out_7[4]), .Qn(t_ff_5_qn), .preset(demultiplexer_5_out1), .reset(or_9_out),
    .en(Enable));
  or or_8 (or_8_out, and_7_out, and_8_out);
  or or_9 (or_9_out, demultiplexer_5_out0, \Сброс );
  Demultiplexer #(.disabled(0)) demultiplexer_5 (
    .out0(demultiplexer_5_out0), .out1(demultiplexer_5_out1), .in(\Запись ), .sel(in_6[4]));  // open: en
  and and_9 (and_9_out, and_7_out, out_7[4]);
  and and_10 (and_10_out, t_ff_5_qn, and_8_out);
  T_Flip_Flop t_ff_6 (
    .clk(Clock), .T(or_10_out), .Q(out_7[5]), .Qn(t_ff_6_qn), .preset(demultiplexer_6_out1),
    .reset(or_11_out), .en(Enable));
  or or_10 (or_10_out, and_9_out, and_10_out);
  or or_11 (or_11_out, demultiplexer_6_out0, \Сброс );
  Demultiplexer #(.disabled(0)) demultiplexer_6 (
    .out0(demultiplexer_6_out0), .out1(demultiplexer_6_out1), .in(\Запись ), .sel(in_6[5]));  // open: en
  and and_11 (and_11_out, and_9_out, out_7[5]);
  and and_12 (and_12_out, t_ff_6_qn, and_10_out);
  T_Flip_Flop t_ff_7 (
    .clk(Clock), .T(or_12_out), .Q(out_7[6]), .Qn(t_ff_7_qn), .preset(demultiplexer_7_out1),
    .reset(or_13_out), .en(Enable));
  or or_12 (or_12_out, and_11_out, and_12_out);
  or or_13 (or_13_out, demultiplexer_7_out0, \Сброс );
  Demultiplexer #(.disabled(0)) demultiplexer_7 (
    .out0(demultiplexer_7_out0), .out1(demultiplexer_7_out1), .in(\Запись ), .sel(in_6[6]));  // open: en
  and and_13 (and_13_out, and_11_out, out_7[6]);
  and and_14 (and_14_out, t_ff_7_qn, and_12_out);
  T_Flip_Flop t_ff_8 (
    .clk(Clock), .T(or_14_out), .Q(out_7[7]), .preset(demultiplexer_8_out1), .reset(or_15_out), .en(Enable));  // open: Qn
  or or_14 (or_14_out, and_13_out, and_14_out);
  or or_15 (or_15_out, demultiplexer_8_out0, \Сброс );
  Demultiplexer #(.disabled(0)) demultiplexer_8 (
    .out0(demultiplexer_8_out0), .out1(demultiplexer_8_out1), .in(\Запись ), .sel(in_6[7]));  // open: en
endmodule

module \Регистр_8_бит  (
  input  in_1,
  input  in_2,
  input  in_3,
  input  [7:0] in_4,
  output [7:0] out_5
);

  D_Flip_Flop d_ff_1 (.clk(in_1), .D(in_4[0]), .Q(out_5[0]), .en(in_3), .reset(in_2));  // open: Qn, preset
  D_Flip_Flop d_ff_2 (.clk(in_1), .D(in_4[1]), .Q(out_5[1]), .en(in_3), .reset(in_2));  // open: Qn, preset
  D_Flip_Flop d_ff_3 (.clk(in_1), .D(in_4[2]), .Q(out_5[2]), .en(in_3), .reset(in_2));  // open: Qn, preset
  D_Flip_Flop d_ff_4 (.clk(in_1), .D(in_4[3]), .Q(out_5[3]), .en(in_3), .reset(in_2));  // open: Qn, preset
  D_Flip_Flop d_ff_5 (.clk(in_1), .D(in_4[4]), .Q(out_5[4]), .en(in_3), .reset(in_2));  // open: Qn, preset
  D_Flip_Flop d_ff_6 (.clk(in_1), .D(in_4[5]), .Q(out_5[5]), .en(in_3), .reset(in_2));  // open: Qn, preset
  D_Flip_Flop d_ff_7 (.clk(in_1), .D(in_4[6]), .Q(out_5[6]), .en(in_3), .reset(in_2));  // open: Qn, preset
  D_Flip_Flop d_ff_8 (.clk(in_1), .D(in_4[7]), .Q(out_5[7]), .en(in_3), .reset(in_2));  // open: Qn, preset
endmodule
